# Fritzing sketch Digital thermometer HC595 (saved by Fritzing 0.9.1b)
breadboards: 1

parts:
  Part1 = Arduino Uno (Rev3) - ICSP
  U1 = TMP36 [package=to-92]
  U2 = 74HC595 [package="DIP16 [THT]"]
  U3 = 74HC595 [package="DIP16 [THT]"]
  U4 = 7-SEGMENT-4DIGIT [package=7-segment-4digit_longpads_for_pogobed]  # not connected

nets:
  N1: Part1.A1, U1.VOUT
  GND: Part1.GND, U1.GND, U2.GND, U2.OE, U3.GND, U3.OE
  N2: Part1.D11_PWM/MOSI, U2.SH_CP, U3.SH_CP
  N3: Part1.D12/MISO, U3.DS
  N4: Part1.D13/SCK, U2.ST_CP, U3.ST_CP
  VCC: Part1.5V, U1.VCC, U2.MR, U2.VCC, U3.MR, U3.VCC
  N5: U2.DS, U3.Q7'
